# Fritzing sketch C6_basic_input (saved by Fritzing 0.8.5b)

parts:
  Raspberry_Pi_B_rev1 = Raspberry Pi B rev2
  S1 = Square Pushbutton

nets:
  N1: Raspberry_Pi_B_rev1.GND, S1.leg1
  N2: Raspberry_Pi_B_rev1.GPIO_17, S1.leg0
