# Fritzing sketch C6_interrupt_input (saved by Fritzing 0.8.5b)
breadboards: 1

parts:
  Raspberry_Pi_B_rev1 = Raspberry Pi B rev2
  R1 = Resistor [tolerance=±5% resistance=220 package=THT]
  LED1 = smd LED [color="Red (633nm)" package="0603 [SMD]"]
  S1 = Square Pushbutton

nets:
  N1: Raspberry_Pi_B_rev1.GND, LED1.cathode, S1.leg1
  N2: Raspberry_Pi_B_rev1.GPIO_17, S1.leg0
  N3: Raspberry_Pi_B_rev1.GPIO_4, R1.Pin_1
  N4: R1.Pin_0, LED1.anode
