# Fritzing sketch C6_multiple_output (saved by Fritzing 0.8.5b)
breadboards: 1

parts:
  Raspberry_Pi_B_rev1 = Raspberry Pi B rev2
  R1 = Resistor [tolerance=±5% resistance=220 package=THT]
  LED1 = smd LED [color="Red (633nm)" package="0603 [SMD]"]
  LED2 = LED - 5mm [color="Red (633nm)" package="5 mm [THT]"]
  R2 = Resistor [tolerance=±5% resistance=220 package=THT]

nets:
  N1: Raspberry_Pi_B_rev1.GND, LED1.cathode, LED2.cathode
  N2: Raspberry_Pi_B_rev1.GPIO_17, R2.Pin_1
  N3: Raspberry_Pi_B_rev1.GPIO_4, R1.Pin_1
  N4: R1.Pin_0, LED1.anode
  N5: LED2.anode, R2.Pin_0
