# Fritzing sketch C7_point-and-shoot-camera (saved by Fritzing 0.8.5b)

parts:
  Raspberry_Pi_B_rev1 = Raspberry Pi B rev2
  S1 = Square Pushbutton
  U1 = SWITCH_SPDT [package=kps-1290]

nets:
  N1: Raspberry_Pi_B_rev1.GND, S1.leg1, U1.P
  N2: Raspberry_Pi_B_rev1.GPIO_17, U1.O
  N3: Raspberry_Pi_B_rev1.GPIO_4, S1.leg0
